// Logisim project FirstVersion.circ as structural Verilog: 23 circuits, main circuit main
module main (
);

  wire carry, carry_in, clock, imr_out_to_a, imr_out_to_b, ir_out_to_a, ir_out_to_b, iren, mar_out_to_a,
       mar_out_to_b, mdr_out_to_a, mdr_out_to_b, negative, negative_in, pc_out_to_a, pc_out_to_b,
       reg_0_out_to_a, reg_0_out_to_b, reg_1_out_to_a, reg_1_out_to_b, reg_2_out_to_a, reg_2_out_to_b,
       reg_3_out_to_a, reg_3_out_to_b, reg_4_out_to_a, reg_4_out_to_b, reg_5_out_to_a, reg_5_out_to_b,
       reg_6_out_to_a, reg_6_out_to_b, reg_7_out_to_a, reg_7_out_to_b, reg_14_out_to_a, reg_14_out_to_b,
       sp_out_to_a, sp_out_to_b, stat_out_to_a, stat_out_to_b, zero, zero_in;
  wire [7:0] instruction, instruction_register;
  wire [15:0] a_bus, address_o, alu_output, b_bus, data_io, immediate_value_q, memory_address_register_q,
       memory_data_register_q, program_counter_q, r0_q, r1_q, r2_q, r3_q, r4_q, r5_q, r6_q, r7_q, r14_q,
       stack_pointer_q, status_register_q;

  Clock clock_1 (.out(clock));
  Decoder #(.select(4)) decoder_1 (
    .out0(reg_0_out_to_a), .out1(reg_1_out_to_a), .out2(reg_2_out_to_a), .out3(reg_3_out_to_a),
    .out4(reg_4_out_to_a), .out5(reg_5_out_to_a), .out6(reg_6_out_to_a), .out7(reg_7_out_to_a),
    .out8(pc_out_to_a), .out9(sp_out_to_a), .out10(stat_out_to_a), .out11(ir_out_to_a), .out12(mar_out_to_a),
    .out13(mdr_out_to_a), .out14(reg_14_out_to_a), .out15(imr_out_to_a), .sel(instruction_register[7:4]));  // open: en
  Decoder #(.select(4)) decoder_2 (
    .out0(reg_0_out_to_b), .out1(reg_1_out_to_b), .out2(reg_2_out_to_b), .out3(reg_3_out_to_b),
    .out4(reg_4_out_to_b), .out5(reg_5_out_to_b), .out6(reg_6_out_to_b), .out7(reg_7_out_to_b),
    .out8(pc_out_to_b), .out9(sp_out_to_b), .out10(stat_out_to_b), .out11(ir_out_to_b), .out12(mar_out_to_b),
    .out13(mdr_out_to_b), .out14(reg_14_out_to_b), .out15(imr_out_to_b), .sel(instruction_register[3:0]));  // open: en
  Register #(.width(16), .Select("low")) r0 (.Q(r0_q), .clk(clock));  // open: D, en, clr
  Register #(.width(16), .Select("low")) r1 (.Q(r1_q), .clk(clock));  // open: D, en, clr
  Register #(.width(16), .Select("low")) r2 (.Q(r2_q), .clk(clock));  // open: D, en, clr
  Register #(.width(16), .Select("low")) r3 (.Q(r3_q), .clk(clock));  // open: D, en, clr
  Register #(.width(16), .Select("low")) r4 (.Q(r4_q), .clk(clock));  // open: D, en, clr
  Register #(.width(16), .Select("low")) r5 (.Q(r5_q), .clk(clock));  // open: D, en, clr
  Register #(.width(16), .Select("low")) r6 (.Q(r6_q), .clk(clock));  // open: D, en, clr
  Register #(.width(16), .Select("low")) r7 (.Q(r7_q), .clk(clock));  // open: D, en, clr
  Counter #(.width(16), .max('hffff)) program_counter (
    .Q(program_counter_q), .clk(clock));  // open: load, D, count, carry, clr, preset, down
  Counter #(.width(16), .max('hffff)) stack_pointer (
    .Q(stack_pointer_q), .clk(clock));  // open: load, D, count, carry, clr, preset, down
  status_register status_register (
    .c(carry_in), .z(zero_in), .n(negative_in), .q(status_register_q), .c_out(carry), .z_out(zero),
    .n_out(negative), .iren_out(iren));  // open: data, clock, iren, write_status, enable
  Register #(.width(16), .Select("low")) u_instruction_register (
    .Q({instruction, instruction_register}), .clk(clock));  // open: D, en, clr
  Register #(.width(16), .Select("low")) memory_address_register (
    .Q(memory_address_register_q), .clk(clock));  // open: D, en, clr
  Register #(.width(16), .Select("low")) memory_data_register (
    .Q(memory_data_register_q), .clk(clock));  // open: D, en, clr
  Register #(.width(16), .Select("low")) r14 (.Q(r14_q), .clk(clock));  // open: D, en, clr
  Register #(.width(16), .Select("low")) immediate_value (.Q(immediate_value_q), .clk(clock));  // open: D, en, clr
  assign a_bus = reg_7_out_to_a ? r7_q : 16'bz;  // Controlled_Buffer controlled_buffer_1
  assign b_bus = reg_7_out_to_b ? r7_q : 16'bz;  // Controlled_Buffer controlled_buffer_2
  assign a_bus = pc_out_to_a ? program_counter_q : 16'bz;  // Controlled_Buffer controlled_buffer_3
  assign b_bus = pc_out_to_b ? program_counter_q : 16'bz;  // Controlled_Buffer controlled_buffer_4
  assign a_bus = sp_out_to_a ? stack_pointer_q : 16'bz;  // Controlled_Buffer controlled_buffer_5
  assign b_bus = sp_out_to_b ? stack_pointer_q : 16'bz;  // Controlled_Buffer controlled_buffer_6
  assign a_bus = mar_out_to_a ? memory_address_register_q : 16'bz;  // Controlled_Buffer controlled_buffer_7
  assign b_bus = mar_out_to_b ? memory_address_register_q : 16'bz;  // Controlled_Buffer controlled_buffer_8
  assign a_bus = mdr_out_to_a ? memory_data_register_q : 16'bz;  // Controlled_Buffer controlled_buffer_9
  assign b_bus = mdr_out_to_b ? memory_data_register_q : 16'bz;  // Controlled_Buffer controlled_buffer_10
  assign a_bus = reg_14_out_to_a ? r14_q : 16'bz;  // Controlled_Buffer controlled_buffer_11
  assign b_bus = reg_14_out_to_b ? r14_q : 16'bz;  // Controlled_Buffer controlled_buffer_12
  assign a_bus = imr_out_to_a ? immediate_value_q : 16'bz;  // Controlled_Buffer controlled_buffer_13
  assign b_bus = imr_out_to_b ? immediate_value_q : 16'bz;  // Controlled_Buffer controlled_buffer_14
  assign a_bus = reg_0_out_to_a ? r0_q : 16'bz;  // Controlled_Buffer controlled_buffer_15
  assign b_bus = reg_0_out_to_b ? r0_q : 16'bz;  // Controlled_Buffer controlled_buffer_16
  assign a_bus = reg_1_out_to_a ? r1_q : 16'bz;  // Controlled_Buffer controlled_buffer_17
  assign b_bus = reg_1_out_to_b ? r1_q : 16'bz;  // Controlled_Buffer controlled_buffer_18
  assign a_bus = reg_2_out_to_a ? r2_q : 16'bz;  // Controlled_Buffer controlled_buffer_19
  assign b_bus = reg_2_out_to_b ? r2_q : 16'bz;  // Controlled_Buffer controlled_buffer_20
  assign a_bus = reg_3_out_to_a ? r3_q : 16'bz;  // Controlled_Buffer controlled_buffer_21
  assign b_bus = reg_3_out_to_b ? r3_q : 16'bz;  // Controlled_Buffer controlled_buffer_22
  assign a_bus = reg_4_out_to_a ? r4_q : 16'bz;  // Controlled_Buffer controlled_buffer_23
  assign b_bus = reg_4_out_to_b ? r4_q : 16'bz;  // Controlled_Buffer controlled_buffer_24
  assign a_bus = reg_5_out_to_a ? r5_q : 16'bz;  // Controlled_Buffer controlled_buffer_25
  assign b_bus = reg_5_out_to_b ? r5_q : 16'bz;  // Controlled_Buffer controlled_buffer_26
  assign a_bus = reg_6_out_to_a ? r6_q : 16'bz;  // Controlled_Buffer controlled_buffer_27
  assign b_bus = reg_6_out_to_b ? r6_q : 16'bz;  // Controlled_Buffer controlled_buffer_28
  assign a_bus = stat_out_to_a ? status_register_q : 16'bz;  // Controlled_Buffer controlled_buffer_29
  assign b_bus = stat_out_to_b ? status_register_q : 16'bz;  // Controlled_Buffer controlled_buffer_30
  assign a_bus = ir_out_to_a ? {instruction, instruction_register} : 16'bz;  // Controlled_Buffer controlled_buffer_31
  assign b_bus = ir_out_to_b ? {instruction, instruction_register} : 16'bz;  // Controlled_Buffer controlled_buffer_32
  alu alu (
    .instruction(instruction), .carry_in(carry), .a(a_bus), .b(b_bus), .output_value(alu_output),
    .zero_out(carry_in), .carry_out(zero_in), .minus_out(negative_in));
  RAM #(.addrWidth(16), .dataWidth(16), .Select("low")) ram_1 (
    .addr(address_o), .data(data_io));  // open: sel, clk, ld, clr

  // Other names for the same wires on the sheet: instruction_register[15:8] = instruction

  // Notes on the sheet:
  //   reg1
  //   reg2
  //   first 8 bits are instruction, next 4 are reg1 final 4 are reg 2
endmodule

module start_to_16_bit_shr (
  input  [15:0] value,
  input  [3:0] shift_amount
);

  wire decoder_1_out1, decoder_1_out2, decoder_1_out3, decoder_1_out4, decoder_1_out5, decoder_1_out6,
       decoder_1_out7, decoder_1_out8, decoder_2_out0, decoder_2_out1, decoder_2_out2, decoder_2_out3,
       decoder_2_out4, decoder_2_out5, decoder_2_out6, decoder_2_out7, decoder_3_out0, decoder_3_out1,
       decoder_3_out2, decoder_3_out3, decoder_3_out4, decoder_3_out5, decoder_3_out6, decoder_4_out0,
       decoder_4_out1, decoder_4_out2, decoder_4_out3, decoder_4_out4, decoder_4_out5, decoder_5_out0,
       decoder_5_out1, decoder_5_out2, decoder_5_out3, decoder_5_out4, decoder_6_out0, decoder_6_out1,
       decoder_6_out2, decoder_6_out3, decoder_7_out0, decoder_7_out1, decoder_7_out2, decoder_8_out0,
       decoder_8_out1, decoder_9_out0;
  wire [8:0] decoder_1_out0;

  Decoder #(.select(4), .disabled(0)) decoder_1 (
    .out0(decoder_1_out0[0]), .out1(decoder_1_out1), .out2(decoder_1_out2), .out3(decoder_1_out3),
    .out4(decoder_1_out4), .out5(decoder_1_out5), .out6(decoder_1_out6), .out7(decoder_1_out7),
    .out8(decoder_1_out8), .sel(shift_amount), .en(value[0]));  // open: out9, out10, out11, out12, out13, out14, out15
  Decoder #(.select(4), .disabled(0)) decoder_2 (
    .out0(decoder_2_out0), .out1(decoder_2_out1), .out2(decoder_2_out2), .out3(decoder_2_out3),
    .out4(decoder_2_out4), .out5(decoder_2_out5), .out6(decoder_2_out6), .out7(decoder_2_out7),
    .sel(shift_amount), .en(value[1]));  // open: out8, out9, out10, out11, out12, out13, out14, out15
  Decoder #(.select(4), .disabled(0)) decoder_3 (
    .out0(decoder_3_out0), .out1(decoder_3_out1), .out2(decoder_3_out2), .out3(decoder_3_out3),
    .out4(decoder_3_out4), .out5(decoder_3_out5), .out6(decoder_3_out6), .sel(shift_amount), .en(value[2]));  // open: out7, out8, out9, out10, out11, out12, out13, out14, out15
  Decoder #(.select(4), .disabled(0)) decoder_4 (
    .out0(decoder_4_out0), .out1(decoder_4_out1), .out2(decoder_4_out2), .out3(decoder_4_out3),
    .out4(decoder_4_out4), .out5(decoder_4_out5), .sel(shift_amount), .en(value[3]));  // open: out6, out7, out8, out9, out10, out11, out12, out13, out14, out15
  Decoder #(.select(4), .disabled(0)) decoder_5 (
    .out0(decoder_5_out0), .out1(decoder_5_out1), .out2(decoder_5_out2), .out3(decoder_5_out3),
    .out4(decoder_5_out4), .sel(shift_amount), .en(value[4]));  // open: out5, out6, out7, out8, out9, out10, out11, out12, out13, out14, out15
  Decoder #(.select(4), .disabled(0)) decoder_6 (
    .out0(decoder_6_out0), .out1(decoder_6_out1), .out2(decoder_6_out2), .out3(decoder_6_out3),
    .sel(shift_amount), .en(value[5]));  // open: out4, out5, out6, out7, out8, out9, out10, out11, out12, out13, out14, out15
  Decoder #(.select(4), .disabled(0)) decoder_7 (
    .out0(decoder_7_out0), .out1(decoder_7_out1), .out2(decoder_7_out2), .sel(shift_amount), .en(value[6]));  // open: out3, out4, out5, out6, out7, out8, out9, out10, out11, out12, out13, out14, out15
  Decoder #(.select(4), .disabled(0)) decoder_8 (
    .out0(decoder_8_out0), .out1(decoder_8_out1), .sel(shift_amount), .en(value[7]));  // open: out2, out3, out4, out5, out6, out7, out8, out9, out10, out11, out12, out13, out14, out15
  Decoder #(.select(4), .disabled(0)) decoder_9 (
    .out0(decoder_9_out0), .sel(shift_amount), .en(value[8]));  // open: out1, out2, out3, out4, out5, out6, out7, out8, out9, out10, out11, out12, out13, out14, out15
  Decoder #(.select(4), .disabled(0)) decoder_10 (
    .sel(shift_amount), .en(value[9]));  // open: out0, out1, out2, out3, out4, out5, out6, out7, out8, out9, out10, out11, out12, out13, out14, out15
  Decoder #(.select(4), .disabled(0)) decoder_11 (
    .sel(shift_amount), .en(value[10]));  // open: out0, out1, out2, out3, out4, out5, out6, out7, out8, out9, out10, out11, out12, out13, out14, out15
  Decoder #(.select(4), .disabled(0)) decoder_12 (
    .sel(shift_amount), .en(value[11]));  // open: out0, out1, out2, out3, out4, out5, out6, out7, out8, out9, out10, out11, out12, out13, out14, out15
  Decoder #(.select(4), .disabled(0)) decoder_13 (
    .sel(shift_amount), .en(value[12]));  // open: out0, out1, out2, out3, out4, out5, out6, out7, out8, out9, out10, out11, out12, out13, out14, out15
  Decoder #(.select(4), .disabled(0)) decoder_14 (
    .sel(shift_amount), .en(value[13]));  // open: out0, out1, out2, out3, out4, out5, out6, out7, out8, out9, out10, out11, out12, out13, out14, out15
  Decoder #(.select(4), .disabled(0)) decoder_15 (
    .sel(shift_amount), .en(value[14]));  // open: out0, out1, out2, out3, out4, out5, out6, out7, out8, out9, out10, out11, out12, out13, out14, out15
  Decoder #(.select(4), .disabled(0)) decoder_16 (
    .sel(shift_amount), .en(value[15]));  // open: out0, out1, out2, out3, out4, out5, out6, out7, out8, out9, out10, out11, out12, out13, out14, out15
  or or_1 (decoder_1_out0[1], decoder_1_out1, decoder_2_out0);
  or or_2 (decoder_1_out0[2], decoder_1_out2, decoder_2_out1, decoder_3_out0);
  or or_3 (decoder_1_out0[3], decoder_1_out3, decoder_2_out2, decoder_3_out1, decoder_4_out0);
  or or_4 (decoder_1_out0[4], decoder_1_out4, decoder_2_out3, decoder_3_out2, decoder_4_out1, decoder_5_out0);
  or or_5 (decoder_1_out0[5], decoder_1_out5, decoder_2_out4, decoder_3_out3, decoder_4_out2, decoder_5_out1, decoder_6_out0);
  or or_6 (decoder_1_out0[6], decoder_1_out6, decoder_2_out5, decoder_3_out4, decoder_4_out3, decoder_5_out2, decoder_6_out1, decoder_7_out0);
  or or_7 (decoder_1_out0[7], decoder_1_out7, decoder_2_out6, decoder_3_out5, decoder_4_out4, decoder_5_out3, decoder_6_out2, decoder_7_out1, decoder_8_out0);
  or or_8 (decoder_1_out0[8], decoder_1_out8, decoder_2_out7, decoder_3_out6, decoder_4_out5, decoder_9_out0, decoder_5_out4, decoder_6_out3, decoder_7_out2, decoder_8_out1);
endmodule

module half_adder (
  input  in_1,
  input  in_2,
  output out_3,
  output out_4
);

  xor xor_1 (out_3, in_1, in_2);
  and and_1 (out_4, in_1, in_2);
endmodule

module full_adder (
  input  in_1,
  input  in_2,
  input  in_3,
  output out_4,
  output out_5
);

  wire half_adder_1_out_3, half_adder_1_out_4, half_adder_2_out_4;

  half_adder half_adder_1 (.in_1(in_1), .in_2(in_2), .out_3(half_adder_1_out_3), .out_4(half_adder_1_out_4));
  half_adder half_adder_2 (.in_1(half_adder_1_out_3), .in_2(in_3), .out_3(out_4), .out_4(half_adder_2_out_4));
  or or_1 (out_5, half_adder_1_out_4, half_adder_2_out_4);
endmodule

module _16_bit_adder (
  input  carry_in,
  input  [15:0] a,
  input  [15:0] b,
  output [15:0] carry_out,
  output carry_out_2
);

  wire full_adder_1_out_5, full_adder_2_out_5, full_adder_3_out_5, full_adder_4_out_5, full_adder_5_out_5,
       full_adder_6_out_5, full_adder_7_out_5, full_adder_8_out_5, full_adder_9_out_5, full_adder_10_out_5,
       full_adder_11_out_5, full_adder_12_out_5, full_adder_13_out_5, full_adder_14_out_5,
       full_adder_15_out_5;

  full_adder full_adder_1 (.in_1(carry_in), .in_2(a[0]), .in_3(b[0]), .out_4(carry_out[0]), .out_5(full_adder_1_out_5));
  full_adder full_adder_2 (
    .in_1(full_adder_1_out_5), .in_2(a[1]), .in_3(b[1]), .out_4(carry_out[1]), .out_5(full_adder_2_out_5));
  full_adder full_adder_3 (
    .in_1(full_adder_2_out_5), .in_2(a[2]), .in_3(b[2]), .out_4(carry_out[2]), .out_5(full_adder_3_out_5));
  full_adder full_adder_4 (
    .in_1(full_adder_3_out_5), .in_2(a[3]), .in_3(b[3]), .out_4(carry_out[3]), .out_5(full_adder_4_out_5));
  full_adder full_adder_5 (
    .in_1(full_adder_4_out_5), .in_2(a[4]), .in_3(b[4]), .out_4(carry_out[4]), .out_5(full_adder_5_out_5));
  full_adder full_adder_6 (
    .in_1(full_adder_5_out_5), .in_2(a[5]), .in_3(b[5]), .out_4(carry_out[5]), .out_5(full_adder_6_out_5));
  full_adder full_adder_7 (
    .in_1(full_adder_6_out_5), .in_2(a[6]), .in_3(b[6]), .out_4(carry_out[6]), .out_5(full_adder_7_out_5));
  full_adder full_adder_8 (
    .in_1(full_adder_7_out_5), .in_2(a[7]), .in_3(b[7]), .out_4(carry_out[7]), .out_5(full_adder_8_out_5));
  full_adder full_adder_9 (
    .in_1(full_adder_8_out_5), .in_2(a[8]), .in_3(b[8]), .out_4(carry_out[8]), .out_5(full_adder_9_out_5));
  full_adder full_adder_10 (
    .in_1(full_adder_9_out_5), .in_2(a[9]), .in_3(b[9]), .out_4(carry_out[9]), .out_5(full_adder_10_out_5));
  full_adder full_adder_11 (
    .in_1(full_adder_10_out_5), .in_2(a[10]), .in_3(b[10]), .out_4(carry_out[10]), .out_5(full_adder_11_out_5));
  full_adder full_adder_12 (
    .in_1(full_adder_11_out_5), .in_2(a[11]), .in_3(b[11]), .out_4(carry_out[11]), .out_5(full_adder_12_out_5));
  full_adder full_adder_13 (
    .in_1(full_adder_12_out_5), .in_2(a[12]), .in_3(b[12]), .out_4(carry_out[12]), .out_5(full_adder_13_out_5));
  full_adder full_adder_14 (
    .in_1(full_adder_13_out_5), .in_2(a[13]), .in_3(b[13]), .out_4(carry_out[13]), .out_5(full_adder_14_out_5));
  full_adder full_adder_15 (
    .in_1(full_adder_14_out_5), .in_2(a[14]), .in_3(b[14]), .out_4(carry_out[14]), .out_5(full_adder_15_out_5));
  full_adder full_adder_16 (
    .in_1(full_adder_15_out_5), .in_2(a[15]), .in_3(b[15]), .out_4(carry_out[15]), .out_5(carry_out_2));
endmodule

module _16_bit_add_sub (
  input  carry,
  input  use_carry,
  input  subtract,
  input  [15:0] a,
  input  [15:0] b,
  output [15:0] \output ,
  output carry_out
);

  wire and_1_out, and_2_out, not_1_out, not_2_out, or_1_out;
  wire [15:0] controlled_inverter_1_out;

  and and_1 (and_1_out, carry, use_carry);
  not not_1 (not_1_out, use_carry);
  assign controlled_inverter_1_out = subtract ? ~b : 16'bz;  // Controlled_Inverter controlled_inverter_1
  assign controlled_inverter_1_out = not_2_out ? b : 16'bz;  // Controlled_Buffer controlled_buffer_1
  not not_2 (not_2_out, subtract);
  and and_2 (and_2_out, not_1_out, subtract);
  or or_1 (or_1_out, and_1_out, and_2_out);
  _16_bit_adder u_16_bit_adder_1 (
    .carry_in(or_1_out), .a(a), .b(controlled_inverter_1_out), .carry_out(\output ), .carry_out_2(carry_out));
  // Probe on a
  // Probe on b
  // Probe on \output 
endmodule

module alu (
  input  [7:0] instruction,
  input  carry_in,
  input  [15:0] a,
  input  [15:0] b,
  output [15:0] output_value,
  output zero_out,
  output carry_out,
  output minus_out
);

  wire decoder_1_out0, decoder_1_out1, decoder_1_out2, decoder_1_out3, decoder_1_out4, decoder_1_out5,
       decoder_1_out6, decoder_1_out7, decoder_1_out8, decoder_1_out9, decoder_1_out10, decoder_1_out11,
       decoder_1_out12, or_2_out;
  wire [15:0] and_1_out, n16_bit_add_sub_1_output, nand_1_out, nor_1_out, or_1_out,
       shiftl_rotatel_16_bit_1_output, shiftr_rotater_16_bit_1_output, xnor_1_out, xor_1_out;

  // Probe on a
  // Probe on b
  // Probe on {minus_out, output_value[14:0]}
  // Probe on {minus_out, output_value[14:0]}
  _16_bit_add_sub u_16_bit_add_sub_1 (
    .carry(carry_in), .use_carry(instruction[0]), .subtract(instruction[1]), .a(a), .b(b),
    .\output (n16_bit_add_sub_1_output), .carry_out(carry_out));
  assign and_1_out = a & b;  // AND_Gate and_1, 16 bits wide
  assign or_1_out = a | b;  // OR_Gate or_1, 16 bits wide
  assign nand_1_out = ~(a & b);  // NAND_Gate nand_1, 16 bits wide
  assign nor_1_out = ~(a | b);  // NOR_Gate nor_1, 16 bits wide
  assign xor_1_out = a ^ b;  // XOR_Gate xor_1, 16 bits wide
  assign xnor_1_out = ~(a ^ b);  // XNOR_Gate xnor_1, 16 bits wide
  shiftR_rotateR_16_bit shiftr_rotater_16_bit_1 (
    .\input (a), .shift_Amount(b[3:0]), .rotate(instruction[0]), .\output (shiftr_rotater_16_bit_1_output));
  shiftL_rotateL_16_bit shiftl_rotatel_16_bit_1 (
    .\input (a), .shift_Amount(b[3:0]), .rotate(instruction[0]), .\output (shiftl_rotatel_16_bit_1_output));
  assign {minus_out, output_value[14:0]} = or_2_out ? n16_bit_add_sub_1_output : 16'bz;  // Controlled_Buffer controlled_buffer_1
  or or_2 (or_2_out, decoder_1_out0, decoder_1_out1, decoder_1_out10, decoder_1_out2, decoder_1_out3);
  assign {minus_out, output_value[14:0]} = decoder_1_out4 ? and_1_out : 16'bz;  // Controlled_Buffer controlled_buffer_2
  assign {minus_out, output_value[14:0]} = decoder_1_out5 ? or_1_out : 16'bz;  // Controlled_Buffer controlled_buffer_3
  assign {minus_out, output_value[14:0]} = decoder_1_out6 ? nand_1_out : 16'bz;  // Controlled_Buffer controlled_buffer_4
  assign {minus_out, output_value[14:0]} = decoder_1_out7 ? nor_1_out : 16'bz;  // Controlled_Buffer controlled_buffer_5
  assign {minus_out, output_value[14:0]} = decoder_1_out8 ? xor_1_out : 16'bz;  // Controlled_Buffer controlled_buffer_6
  assign {minus_out, output_value[14:0]} = decoder_1_out9 ? xnor_1_out : 16'bz;  // Controlled_Buffer controlled_buffer_7
  assign {minus_out, output_value[14:0]} = decoder_1_out11 ? shiftr_rotater_16_bit_1_output : 16'bz;  // Controlled_Buffer controlled_buffer_8
  assign {minus_out, output_value[14:0]} = decoder_1_out12 ? shiftl_rotatel_16_bit_1_output : 16'bz;  // Controlled_Buffer controlled_buffer_9
  Decoder #(.select(4), .enable("false")) decoder_1 (
    .out0(decoder_1_out0), .out1(decoder_1_out1), .out2(decoder_1_out2), .out3(decoder_1_out3),
    .out4(decoder_1_out4), .out5(decoder_1_out5), .out6(decoder_1_out6), .out7(decoder_1_out7),
    .out8(decoder_1_out8), .out9(decoder_1_out9), .out10(decoder_1_out10), .out11(decoder_1_out11),
    .out12(decoder_1_out12), .sel(instruction[5:2]));  // open: out13, out14, out15
  is_zero is_zero_1 (.in_1({minus_out, output_value[14:0]}), .out_2(zero_out));

  assign output_value[15] = minus_out;
endmodule

module is_zero (
  input  [15:0] in_1,
  output out_2
);

  wire or_1_out;

  or or_1 (or_1_out, in_1[0], in_1[1], in_1[2], in_1[3], in_1[4], in_1[5], in_1[6], in_1[7], in_1[8], in_1[9], in_1[10], in_1[11], in_1[12], in_1[13], in_1[14], in_1[15]);
  not not_1 (out_2, or_1_out);
endmodule

module barrel_shifter (
  input  [3:0] a,
  input  [1:0] shift_amount,
  output [3:0] a_2
);

  wire decoder_1_out0, decoder_1_out1, decoder_1_out2, decoder_1_out3;

  Decoder #(.select(2), .enable("false")) decoder_1 (
    .out0(decoder_1_out0), .out1(decoder_1_out1), .out2(decoder_1_out2), .out3(decoder_1_out3),
    .sel(shift_amount));
  assign a_2[3] = decoder_1_out3 ? a[0] : 1'bz;  // Controlled_Buffer controlled_buffer_1
  assign a_2[2] = decoder_1_out2 ? a[0] : 1'bz;  // Controlled_Buffer controlled_buffer_2
  assign a_2[1] = decoder_1_out1 ? a[0] : 1'bz;  // Controlled_Buffer controlled_buffer_3
  assign a_2[0] = decoder_1_out0 ? a[0] : 1'bz;  // Controlled_Buffer controlled_buffer_4
  assign a_2[3] = decoder_1_out2 ? a[1] : 1'bz;  // Controlled_Buffer controlled_buffer_5
  assign a_2[2] = decoder_1_out1 ? a[1] : 1'bz;  // Controlled_Buffer controlled_buffer_6
  assign a_2[1] = decoder_1_out0 ? a[1] : 1'bz;  // Controlled_Buffer controlled_buffer_7
  assign a_2[0] = decoder_1_out3 ? a[1] : 1'bz;  // Controlled_Buffer controlled_buffer_8
  assign a_2[3] = decoder_1_out1 ? a[2] : 1'bz;  // Controlled_Buffer controlled_buffer_9
  assign a_2[2] = decoder_1_out0 ? a[2] : 1'bz;  // Controlled_Buffer controlled_buffer_10
  assign a_2[1] = decoder_1_out3 ? a[2] : 1'bz;  // Controlled_Buffer controlled_buffer_11
  assign a_2[0] = decoder_1_out2 ? a[2] : 1'bz;  // Controlled_Buffer controlled_buffer_12
  assign a_2[3] = decoder_1_out0 ? a[3] : 1'bz;  // Controlled_Buffer controlled_buffer_13
  assign a_2[2] = decoder_1_out3 ? a[3] : 1'bz;  // Controlled_Buffer controlled_buffer_14
  assign a_2[1] = decoder_1_out2 ? a[3] : 1'bz;  // Controlled_Buffer controlled_buffer_15
  assign a_2[0] = decoder_1_out1 ? a[3] : 1'bz;  // Controlled_Buffer controlled_buffer_16
endmodule

module shiftR_rotateR_16_bit (
  input  [15:0] \input ,
  input  [3:0] shift_Amount,
  input  rotate,
  output [15:0] \output 
);

  wire not_1_out;
  wire [15:0] shifter_1_out, shifter_2_out;

  Shifter #(.width(16), .shift("lr")) shifter_1 (.in(\input ), .\dist (shift_Amount), .out(shifter_1_out));
  Shifter #(.width(16), .shift("rr")) shifter_2 (.in(\input ), .\dist (shift_Amount), .out(shifter_2_out));
  assign \output  = not_1_out ? shifter_1_out : 16'bz;  // Controlled_Buffer controlled_buffer_1
  not not_1 (not_1_out, rotate);
  assign \output  = rotate ? shifter_2_out : 16'bz;  // Controlled_Buffer controlled_buffer_2
endmodule

module barrel_shifter_v2 (
  input  [2:0] shift_amount,
  input  rotate,
  input  [7:0] input_number,
  output [7:0] out_4
);

  wire and_2_out, and_3_out, and_4_out, and_5_out, and_6_out, and_7_out, and_8_out, decoder_1_out0,
       decoder_1_out1, decoder_1_out2, decoder_1_out3, decoder_1_out4, decoder_1_out5, decoder_1_out6,
       decoder_1_out7;

  Decoder #(.select(3), .enable("false")) decoder_1 (
    .out0(decoder_1_out0), .out1(decoder_1_out1), .out2(decoder_1_out2), .out3(decoder_1_out3),
    .out4(decoder_1_out4), .out5(decoder_1_out5), .out6(decoder_1_out6), .out7(decoder_1_out7),
    .sel(shift_amount));
  // AND_Gate and_1 has open pins: in0=decoder_1_out0, in1=rotate, out=open
  and and_2 (and_2_out, decoder_1_out1, rotate);
  and and_3 (and_3_out, decoder_1_out2, rotate);
  and and_4 (and_4_out, decoder_1_out3, rotate);
  and and_5 (and_5_out, decoder_1_out4, rotate);
  and and_6 (and_6_out, decoder_1_out5, rotate);
  and and_7 (and_7_out, decoder_1_out6, rotate);
  and and_8 (and_8_out, decoder_1_out7, rotate);
  assign out_4[0] = decoder_1_out0 ? input_number[0] : 1'bz;  // Controlled_Buffer controlled_buffer_1
  assign out_4[1] = decoder_1_out0 ? input_number[1] : 1'bz;  // Controlled_Buffer controlled_buffer_2
  assign out_4[2] = decoder_1_out0 ? input_number[2] : 1'bz;  // Controlled_Buffer controlled_buffer_3
  assign out_4[3] = decoder_1_out0 ? input_number[3] : 1'bz;  // Controlled_Buffer controlled_buffer_4
  assign out_4[4] = decoder_1_out0 ? input_number[4] : 1'bz;  // Controlled_Buffer controlled_buffer_5
  assign out_4[5] = decoder_1_out0 ? input_number[5] : 1'bz;  // Controlled_Buffer controlled_buffer_6
  assign out_4[6] = decoder_1_out0 ? input_number[6] : 1'bz;  // Controlled_Buffer controlled_buffer_7
  assign out_4[7] = decoder_1_out0 ? input_number[7] : 1'bz;  // Controlled_Buffer controlled_buffer_8
  assign out_4[0] = and_2_out ? input_number[7] : 1'bz;  // Controlled_Buffer controlled_buffer_9
  assign out_4[1] = decoder_1_out1 ? input_number[0] : 1'bz;  // Controlled_Buffer controlled_buffer_10
  assign out_4[2] = decoder_1_out1 ? input_number[1] : 1'bz;  // Controlled_Buffer controlled_buffer_11
  assign out_4[3] = decoder_1_out1 ? input_number[2] : 1'bz;  // Controlled_Buffer controlled_buffer_12
  assign out_4[4] = decoder_1_out1 ? input_number[3] : 1'bz;  // Controlled_Buffer controlled_buffer_13
  assign out_4[5] = decoder_1_out1 ? input_number[4] : 1'bz;  // Controlled_Buffer controlled_buffer_14
  assign out_4[6] = decoder_1_out1 ? input_number[5] : 1'bz;  // Controlled_Buffer controlled_buffer_15
  assign out_4[7] = decoder_1_out1 ? input_number[6] : 1'bz;  // Controlled_Buffer controlled_buffer_16
  assign out_4[0] = and_3_out ? input_number[6] : 1'bz;  // Controlled_Buffer controlled_buffer_17
  assign out_4[1] = and_3_out ? input_number[7] : 1'bz;  // Controlled_Buffer controlled_buffer_18
  assign out_4[2] = decoder_1_out2 ? input_number[0] : 1'bz;  // Controlled_Buffer controlled_buffer_19
  assign out_4[3] = decoder_1_out2 ? input_number[1] : 1'bz;  // Controlled_Buffer controlled_buffer_20
  assign out_4[4] = decoder_1_out2 ? input_number[2] : 1'bz;  // Controlled_Buffer controlled_buffer_21
  assign out_4[5] = decoder_1_out2 ? input_number[3] : 1'bz;  // Controlled_Buffer controlled_buffer_22
  assign out_4[6] = decoder_1_out2 ? input_number[4] : 1'bz;  // Controlled_Buffer controlled_buffer_23
  assign out_4[7] = decoder_1_out2 ? input_number[5] : 1'bz;  // Controlled_Buffer controlled_buffer_24
  assign out_4[0] = and_4_out ? input_number[5] : 1'bz;  // Controlled_Buffer controlled_buffer_25
  assign out_4[1] = and_4_out ? input_number[6] : 1'bz;  // Controlled_Buffer controlled_buffer_26
  assign out_4[2] = and_4_out ? input_number[7] : 1'bz;  // Controlled_Buffer controlled_buffer_27
  assign out_4[3] = decoder_1_out3 ? input_number[0] : 1'bz;  // Controlled_Buffer controlled_buffer_28
  assign out_4[4] = decoder_1_out3 ? input_number[1] : 1'bz;  // Controlled_Buffer controlled_buffer_29
  assign out_4[5] = decoder_1_out3 ? input_number[2] : 1'bz;  // Controlled_Buffer controlled_buffer_30
  assign out_4[6] = decoder_1_out3 ? input_number[3] : 1'bz;  // Controlled_Buffer controlled_buffer_31
  assign out_4[7] = decoder_1_out3 ? input_number[4] : 1'bz;  // Controlled_Buffer controlled_buffer_32
  assign out_4[0] = and_5_out ? input_number[4] : 1'bz;  // Controlled_Buffer controlled_buffer_33
  assign out_4[1] = and_5_out ? input_number[5] : 1'bz;  // Controlled_Buffer controlled_buffer_34
  assign out_4[2] = and_5_out ? input_number[6] : 1'bz;  // Controlled_Buffer controlled_buffer_35
  assign out_4[3] = and_5_out ? input_number[7] : 1'bz;  // Controlled_Buffer controlled_buffer_36
  assign out_4[4] = decoder_1_out4 ? input_number[0] : 1'bz;  // Controlled_Buffer controlled_buffer_37
  assign out_4[5] = decoder_1_out4 ? input_number[1] : 1'bz;  // Controlled_Buffer controlled_buffer_38
  assign out_4[6] = decoder_1_out4 ? input_number[2] : 1'bz;  // Controlled_Buffer controlled_buffer_39
  assign out_4[7] = decoder_1_out4 ? input_number[3] : 1'bz;  // Controlled_Buffer controlled_buffer_40
  assign out_4[0] = and_6_out ? input_number[3] : 1'bz;  // Controlled_Buffer controlled_buffer_41
  assign out_4[1] = and_6_out ? input_number[4] : 1'bz;  // Controlled_Buffer controlled_buffer_42
  assign out_4[2] = and_6_out ? input_number[5] : 1'bz;  // Controlled_Buffer controlled_buffer_43
  assign out_4[3] = and_6_out ? input_number[6] : 1'bz;  // Controlled_Buffer controlled_buffer_44
  assign out_4[4] = and_6_out ? input_number[7] : 1'bz;  // Controlled_Buffer controlled_buffer_45
  assign out_4[5] = decoder_1_out5 ? input_number[0] : 1'bz;  // Controlled_Buffer controlled_buffer_46
  assign out_4[6] = decoder_1_out5 ? input_number[1] : 1'bz;  // Controlled_Buffer controlled_buffer_47
  assign out_4[7] = decoder_1_out5 ? input_number[2] : 1'bz;  // Controlled_Buffer controlled_buffer_48
  assign out_4[0] = and_7_out ? input_number[2] : 1'bz;  // Controlled_Buffer controlled_buffer_49
  assign out_4[1] = and_7_out ? input_number[3] : 1'bz;  // Controlled_Buffer controlled_buffer_50
  assign out_4[2] = and_7_out ? input_number[4] : 1'bz;  // Controlled_Buffer controlled_buffer_51
  assign out_4[3] = and_7_out ? input_number[5] : 1'bz;  // Controlled_Buffer controlled_buffer_52
  assign out_4[4] = and_7_out ? input_number[6] : 1'bz;  // Controlled_Buffer controlled_buffer_53
  assign out_4[5] = and_7_out ? input_number[7] : 1'bz;  // Controlled_Buffer controlled_buffer_54
  assign out_4[6] = decoder_1_out6 ? input_number[0] : 1'bz;  // Controlled_Buffer controlled_buffer_55
  assign out_4[7] = decoder_1_out6 ? input_number[1] : 1'bz;  // Controlled_Buffer controlled_buffer_56
  assign out_4[0] = and_8_out ? input_number[1] : 1'bz;  // Controlled_Buffer controlled_buffer_57
  assign out_4[1] = and_8_out ? input_number[2] : 1'bz;  // Controlled_Buffer controlled_buffer_58
  assign out_4[2] = and_8_out ? input_number[3] : 1'bz;  // Controlled_Buffer controlled_buffer_59
  assign out_4[3] = and_8_out ? input_number[4] : 1'bz;  // Controlled_Buffer controlled_buffer_60
  assign out_4[4] = and_8_out ? input_number[5] : 1'bz;  // Controlled_Buffer controlled_buffer_61
  assign out_4[5] = and_8_out ? input_number[6] : 1'bz;  // Controlled_Buffer controlled_buffer_62
  assign out_4[6] = and_8_out ? input_number[7] : 1'bz;  // Controlled_Buffer controlled_buffer_63
  assign out_4[7] = decoder_1_out7 ? input_number[0] : 1'bz;  // Controlled_Buffer controlled_buffer_64
endmodule

module shiftL_rotateL_16_bit (
  input  [15:0] \input ,
  input  [3:0] shift_Amount,
  input  rotate,
  output [15:0] \output 
);

  wire not_1_out;
  wire [15:0] shifter_1_out, shifter_2_out;

  Shifter #(.width(16)) shifter_1 (.in(\input ), .\dist (shift_Amount), .out(shifter_1_out));
  Shifter #(.width(16), .shift("rl")) shifter_2 (.in(\input ), .\dist (shift_Amount), .out(shifter_2_out));
  assign \output  = not_1_out ? shifter_1_out : 16'bz;  // Controlled_Buffer controlled_buffer_1
  not not_1 (not_1_out, rotate);
  assign \output  = rotate ? shifter_2_out : 16'bz;  // Controlled_Buffer controlled_buffer_2
endmodule

module status_register (
  input  [15:0] data,
  input  clock,
  input  c,
  input  z,
  input  n,
  input  iren,
  input  write_status,
  input  enable,
  output [15:0] q,
  output c_out,
  output z_out,
  output n_out,
  output iren_out
);

  wire controlled_buffer_1_out, controlled_buffer_2_out, controlled_buffer_3_out, controlled_buffer_4_out,
       not_1_out;

  assign controlled_buffer_1_out = write_status ? c : 1'bz;  // Controlled_Buffer controlled_buffer_1
  assign controlled_buffer_2_out = write_status ? z : 1'bz;  // Controlled_Buffer controlled_buffer_2
  assign controlled_buffer_3_out = write_status ? n : 1'bz;  // Controlled_Buffer controlled_buffer_3
  assign controlled_buffer_4_out = write_status ? iren : 1'bz;  // Controlled_Buffer controlled_buffer_4
  not not_1 (not_1_out, write_status);
  assign controlled_buffer_1_out = not_1_out ? data[0] : 1'bz;  // Controlled_Buffer controlled_buffer_5
  assign controlled_buffer_2_out = not_1_out ? data[1] : 1'bz;  // Controlled_Buffer controlled_buffer_6
  assign controlled_buffer_3_out = not_1_out ? data[2] : 1'bz;  // Controlled_Buffer controlled_buffer_7
  assign controlled_buffer_4_out = not_1_out ? data[3] : 1'bz;  // Controlled_Buffer controlled_buffer_8
  Register #(.width(1), .Select("low")) register_1 (
    .D(controlled_buffer_1_out), .en(enable), .Q(c_out), .clk(clock));  // open: clr
  Register #(.width(1), .Select("low")) register_2 (
    .D(controlled_buffer_2_out), .en(enable), .Q(q[1]), .clk(clock));  // open: clr
  Register #(.width(1), .Select("low")) register_3 (
    .D(controlled_buffer_3_out), .en(enable), .Q(n_out), .clk(clock));  // open: clr
  Register #(.width(1), .Select("low")) register_4 (
    .D(controlled_buffer_4_out), .en(enable), .Q(iren_out), .clk(clock));  // open: clr
  Register #(.width(1), .Select("low")) register_5 (.D(data[4]), .en(enable), .Q(q[4]), .clk(clock));  // open: clr
  Register #(.width(1), .Select("low")) register_6 (.D(data[5]), .en(enable), .Q(q[5]), .clk(clock));  // open: clr
  Register #(.width(1), .Select("low")) register_7 (.D(data[6]), .en(enable), .Q(q[6]), .clk(clock));  // open: clr
  Register #(.width(1), .Select("low")) register_8 (.D(data[7]), .en(enable), .Q(q[7]), .clk(clock));  // open: clr
  Register #(.Select("low")) register_9 (.D(data[15:8]), .en(enable), .Q(q[15:8]));  // open: clk, clr

  assign {q[3:2], q[0]} = {iren_out, n_out, c_out};
  assign z_out = q[1];
endmodule

module _4_bit_mult (
  input  [3:0] in_1,
  input  [3:0] in_2,
  output [7:0] out_3
);

  wire adder_1_cout, adder_2_cout;
  wire [3:0] and_1_out;
  wire [4:1] and_5_out;
  wire [5:2] and_9_out;
  wire [6:3] and_13_out;
  wire [7:0] adder_1_out, adder_2_out;

  // Probe on in_1
  // Probe on in_2
  and and_1 (and_1_out[0], in_1[0], in_2[0]);
  and and_2 (and_1_out[1], in_1[1], in_2[0]);
  and and_3 (and_1_out[2], in_1[2], in_2[0]);
  and and_4 (and_1_out[3], in_1[3], in_2[0]);
  and and_5 (and_5_out[1], in_1[0], in_2[1]);
  and and_6 (and_5_out[2], in_1[1], in_2[1]);
  and and_7 (and_5_out[3], in_1[2], in_2[1]);
  and and_8 (and_5_out[4], in_1[3], in_2[1]);
  and and_9 (and_9_out[2], in_1[0], in_2[2]);
  and and_10 (and_9_out[3], in_1[1], in_2[2]);
  and and_11 (and_9_out[4], in_1[2], in_2[2]);
  and and_12 (and_9_out[5], in_1[3], in_2[2]);
  and and_13 (and_13_out[3], in_1[0], in_2[3]);
  and and_14 (and_13_out[4], in_1[1], in_2[3]);
  and and_15 (and_13_out[5], in_1[2], in_2[3]);
  and and_16 (and_13_out[6], in_1[3], in_2[3]);
  Adder adder_1 (
    .a({4'b0000, and_1_out}), .b({3'b000, and_5_out, 1'b0}), .out(adder_1_out), .cout(adder_1_cout));  // open: cin
  Adder adder_2 (
    .a(adder_1_out), .b({2'b00, and_9_out, 2'b00}), .out(adder_2_out), .cin(adder_1_cout), .cout(adder_2_cout));
  // Probe on out_3
  Adder adder_3 (.a(adder_2_out), .b({1'b0, and_13_out, 3'b000}), .out(out_3), .cin(adder_2_cout));  // open: cout
endmodule

module controlled_number_negator (
  input  [15:0] Number,
  input  negate,
  output [15:0] out_3
);

  wire not_2_out;
  wire [15:0] adder_1_out, not_1_out;

  // Probe on Number
  assign not_1_out = ~Number;  // NOT_Gate not_1, 16 bits wide
  Adder #(.width(16)) adder_1 (.a(not_1_out), .b({16{1'b0}}), .out(adder_1_out), .cin(1'b1));  // open: cout
  assign out_3 = not_2_out ? Number : 16'bz;  // Controlled_Buffer controlled_buffer_1
  not not_2 (not_2_out, negate);
  assign out_3 = negate ? adder_1_out : 16'bz;  // Controlled_Buffer controlled_buffer_2
  // Probe on out_3
endmodule

module _4_bit_unsigned_multiplier_using_rom (
  input  [3:0] a,
  input  [3:0] b,
  output [7:0] b_2
);

  // Probe on a
  // Probe on b
  ROM #(.Select("low")) rom_1 (.addr({b, a}), .data(b_2));
  // Probe on b_2

  // Notes on the sheet:
  //   contents of rom_1 (hex, n*v repeats v):
  //   17*0 1 2 3 4 5 6 7 8 9 a b c d e f 0 2 4 6 8 a c e 10 12 14 16 18 1a 1c 1e 0 3 6 9 c f 12 15 18 1b
  //   1e 21 24 27 2a 2d 0 4 8 c 10 14 18 1c 20 24 28 2c 30 34 38 3c 0 5 a f 14 19 1e 23 28 2d 32 37 3c 41
  //   46 4b 0 6 c 12 18 1e 24 2a 30 36 3c 42 48 4e 54 5a 0 7 e 15 1c 23 2a 31 38 3f 46 4d 54 5b 62 69 0 8
  //   10 18 20 28 30 38 40 48 50 58 60 68 70 78 0 9 12 1b 24 2d 36 3f 48 51 5a 63 6c 75 7e 87 0 a 14 1e 28
  //   32 3c 46 50 5a 64 6e 78 82 8c 96 0 b 16 21 2c 37 42 4d 58 63 6e 79 84 8f 9a a5 0 c 18 24 30 3c 48 54
  //   60 6c 78 84 90 9c a8 b4 0 d 1a 27 34 41 4e 5b 68 75 82 8f 9c a9 b6 c3 0 e 1c 2a 38 46 54 62 70 7e 8c
  //   9a a8 b6 c4 d2 0 f 1e 2d 3c 4b 5a 69 78 87 96 a5 b4 c3 d2 e1
endmodule

module _8_bit_unsigned_multiplier_using_rom (
  input  [7:0] a,
  input  [7:0] b,
  output [15:0] out_3
);

  wire adder_1_cout, adder_3_cout, adder_5_cout, adder_6_cout;
  wire [3:0] adder_1_out, adder_2_out, adder_3_out, adder_4_out;
  wire [7:0] n4_bit_unsigned_multiplier_using_rom_2_b_2, n4_bit_unsigned_multiplier_using_rom_3_b_2,
       n4_bit_unsigned_multiplier_using_rom_4_b_2;
  wire [7:4] n4_bit_unsigned_multiplier_using_rom_1_b_2;

  // Probe on a
  // Probe on b
  _4_bit_unsigned_multiplier_using_rom u_4_bit_unsigned_multiplier_using_rom_1 (
    .a(a[3:0]), .b(b[3:0]), .b_2({n4_bit_unsigned_multiplier_using_rom_1_b_2, out_3[3:0]}));
  _4_bit_unsigned_multiplier_using_rom u_4_bit_unsigned_multiplier_using_rom_2 (
    .a(a[7:4]), .b(b[3:0]), .b_2(n4_bit_unsigned_multiplier_using_rom_2_b_2));
  _4_bit_unsigned_multiplier_using_rom u_4_bit_unsigned_multiplier_using_rom_3 (
    .a(a[3:0]), .b(b[7:4]), .b_2(n4_bit_unsigned_multiplier_using_rom_3_b_2));
  _4_bit_unsigned_multiplier_using_rom u_4_bit_unsigned_multiplier_using_rom_4 (
    .a(a[7:4]), .b(b[7:4]), .b_2(n4_bit_unsigned_multiplier_using_rom_4_b_2));
  Adder #(.width(4)) adder_1 (
    .a(n4_bit_unsigned_multiplier_using_rom_1_b_2), .b(n4_bit_unsigned_multiplier_using_rom_2_b_2[3:0]),
    .out(adder_1_out), .cout(adder_1_cout));  // open: cin
  Adder #(.width(4)) adder_2 (
    .a(n4_bit_unsigned_multiplier_using_rom_2_b_2[7:4]), .b(4'b0000), .out(adder_2_out), .cin(adder_1_cout));  // open: cout
  Adder #(.width(4)) adder_3 (
    .a(n4_bit_unsigned_multiplier_using_rom_3_b_2[7:4]), .b(n4_bit_unsigned_multiplier_using_rom_4_b_2[3:0]),
    .out(adder_3_out), .cout(adder_3_cout));  // open: cin
  // Probe on nothing
  Adder #(.width(4)) adder_4 (
    .a(n4_bit_unsigned_multiplier_using_rom_4_b_2[7:4]), .b(4'b0000), .out(adder_4_out), .cin(adder_3_cout));  // open: cout
  Adder #(.width(4)) adder_5 (
    .a(adder_1_out), .b(n4_bit_unsigned_multiplier_using_rom_3_b_2[3:0]), .out(out_3[7:4]),
    .cout(adder_5_cout));  // open: cin
  Adder #(.width(4)) adder_6 (
    .a(adder_2_out), .b(adder_3_out), .out(out_3[11:8]), .cin(adder_5_cout), .cout(adder_6_cout));
  Adder #(.width(4)) adder_7 (.a(adder_4_out), .b(4'b0000), .out(out_3[15:12]), .cin(adder_6_cout));  // open: cout
  // Probe on out_3
endmodule

module signed_8_bit_mult_using_rom (
  input  [7:0] in_1,
  input  [7:0] in_2,
  output [15:0] out_3
);

  wire xor_1_out;
  wire [7:0] n8_bit_abs_1_out_2, n8_bit_abs_2_out_2;
  wire [15:0] n8_bit_unsigned_multiplier_using_rom_1_out_3;

  // Probe on in_1
  // Probe on in_2
  _8_bit_abs u_8_bit_abs_1 (.in_1(in_1), .out_2(n8_bit_abs_1_out_2));
  _8_bit_abs u_8_bit_abs_2 (.in_1(in_2), .out_2(n8_bit_abs_2_out_2));
  _8_bit_unsigned_multiplier_using_rom u_8_bit_unsigned_multiplier_using_rom_1 (
    .a(n8_bit_abs_1_out_2), .b(n8_bit_abs_2_out_2), .out_3(n8_bit_unsigned_multiplier_using_rom_1_out_3));
  xor xor_1 (xor_1_out, in_1[7], in_2[7]);
  // Probe on out_3
  controlled_number_negator controlled_number_negator_1 (
    .Number(n8_bit_unsigned_multiplier_using_rom_1_out_3), .negate(xor_1_out), .out_3(out_3));
endmodule

module _8_bit_abs (
  input  [7:0] in_1,
  output [7:0] out_2
);

  wire not_2_out;
  wire [7:0] adder_1_out, not_1_out;

  // Probe on in_1
  assign not_1_out = ~in_1;  // NOT_Gate not_1, 8 bits wide
  not not_2 (not_2_out, in_1[7]);
  Adder adder_1 (.a(not_1_out), .b(8'h1), .out(adder_1_out));  // open: cin, cout
  // Probe on out_2
  assign out_2 = not_2_out ? in_1 : 8'bz;  // Controlled_Buffer controlled_buffer_1
  assign out_2 = in_1[7] ? adder_1_out : 8'bz;  // Controlled_Buffer controlled_buffer_2
endmodule

module s_u_8_bit_mult_using_rom (
  input  [7:0] in_1,
  input  [7:0] in_2,
  input  \signed ,
  output [15:0] out_4
);

  wire not_1_out, xor_1_out;
  wire [7:0] controlled_buffer_1_out, controlled_buffer_3_out, n8_bit_abs_1_out_2, n8_bit_abs_2_out_2;
  wire [15:0] controlled_number_negator_1_out_3, n8_bit_unsigned_multiplier_using_rom_1_out_3;

  // Probe on in_1
  // Probe on in_1
  // Probe on in_2
  // Probe on in_2
  _8_bit_abs u_8_bit_abs_1 (.in_1(in_1), .out_2(n8_bit_abs_1_out_2));
  assign controlled_buffer_1_out = \signed  ? n8_bit_abs_1_out_2 : 8'bz;  // Controlled_Buffer controlled_buffer_1
  assign controlled_buffer_1_out = not_1_out ? in_1 : 8'bz;  // Controlled_Buffer controlled_buffer_2
  assign controlled_buffer_3_out = \signed  ? n8_bit_abs_2_out_2 : 8'bz;  // Controlled_Buffer controlled_buffer_3
  _8_bit_abs u_8_bit_abs_2 (.in_1(in_2), .out_2(n8_bit_abs_2_out_2));
  assign controlled_buffer_3_out = not_1_out ? in_2 : 8'bz;  // Controlled_Buffer controlled_buffer_4
  not not_1 (not_1_out, \signed );
  _8_bit_unsigned_multiplier_using_rom u_8_bit_unsigned_multiplier_using_rom_1 (
    .a(controlled_buffer_1_out), .b(controlled_buffer_3_out),
    .out_3(n8_bit_unsigned_multiplier_using_rom_1_out_3));
  xor xor_1 (xor_1_out, in_1[7], in_2[7]);
  controlled_number_negator controlled_number_negator_1 (
    .Number(n8_bit_unsigned_multiplier_using_rom_1_out_3), .negate(xor_1_out),
    .out_3(controlled_number_negator_1_out_3));
  assign out_4 = not_1_out ? n8_bit_unsigned_multiplier_using_rom_1_out_3 : 16'bz;  // Controlled_Buffer controlled_buffer_5
  // Probe on out_4
  assign out_4 = \signed  ? controlled_number_negator_1_out_3 : 16'bz;  // Controlled_Buffer controlled_buffer_6
  // Probe on out_4
endmodule

module division_circuit_block (
  input  [15:0] \output ,
  input  [15:0] \input ,
  input  [15:0] divisor_h,
  input  [15:0] divisor_l,
  output [15:0] output_value,
  output [15:0] input_output,
  output [15:0] divisor_h_output,
  output [15:0] divisor_l_output
);

  wire not_2_out;
  wire [15:0] adder_1_out, not_1_out;
  wire [15:15] controlled_buffer_1_out;

  assign not_1_out = ~\input ;  // NOT_Gate not_1, 16 bits wide
  Adder #(.width(16)) adder_1 (.a(not_1_out), .b(divisor_h), .out(adder_1_out), .cin(1'b1), .cout(output_value[0]));
  assign {controlled_buffer_1_out[15], divisor_h_output[15:1]} = output_value[0] ? adder_1_out : 16'bz;  // Controlled_Buffer controlled_buffer_1
  assign {controlled_buffer_1_out[15], divisor_h_output[15:1]} = not_2_out ? divisor_h : 16'bz;  // Controlled_Buffer controlled_buffer_2
  not not_2 (not_2_out, output_value[0]);

  assign divisor_h_output[0] = divisor_l[15];
  assign divisor_l_output = {divisor_l[14:0], 1'b0};
  assign input_output = \input ;
  assign output_value[15:1] = \output [14:0];
endmodule

module _16_bit_unsigned_division_circuit (
  input  [15:0] \input ,
  input  [15:0] divisor,
  output [15:0] \output 
);

  wire [15:0] division_circuit_block_1_divisor_h_output, division_circuit_block_1_divisor_l_output,
       division_circuit_block_1_input_output, division_circuit_block_1_output_value,
       division_circuit_block_2_divisor_h_output, division_circuit_block_2_divisor_l_output,
       division_circuit_block_2_input_output, division_circuit_block_2_output_value,
       division_circuit_block_3_divisor_h_output, division_circuit_block_3_divisor_l_output,
       division_circuit_block_3_input_output, division_circuit_block_3_output_value,
       division_circuit_block_4_divisor_h_output, division_circuit_block_4_divisor_l_output,
       division_circuit_block_4_input_output, division_circuit_block_4_output_value,
       division_circuit_block_5_divisor_h_output, division_circuit_block_5_divisor_l_output,
       division_circuit_block_5_input_output, division_circuit_block_5_output_value,
       division_circuit_block_6_divisor_h_output, division_circuit_block_6_divisor_l_output,
       division_circuit_block_6_input_output, division_circuit_block_6_output_value,
       division_circuit_block_7_divisor_h_output, division_circuit_block_7_divisor_l_output,
       division_circuit_block_7_input_output, division_circuit_block_7_output_value,
       division_circuit_block_8_divisor_h_output, division_circuit_block_8_divisor_l_output,
       division_circuit_block_8_input_output, division_circuit_block_8_output_value,
       division_circuit_block_9_divisor_h_output, division_circuit_block_9_divisor_l_output,
       division_circuit_block_9_input_output, division_circuit_block_9_output_value,
       division_circuit_block_10_divisor_h_output, division_circuit_block_10_divisor_l_output,
       division_circuit_block_10_input_output, division_circuit_block_10_output_value,
       division_circuit_block_11_divisor_h_output, division_circuit_block_11_divisor_l_output,
       division_circuit_block_11_input_output, division_circuit_block_11_output_value,
       division_circuit_block_12_divisor_h_output, division_circuit_block_12_divisor_l_output,
       division_circuit_block_12_input_output, division_circuit_block_12_output_value,
       division_circuit_block_13_divisor_h_output, division_circuit_block_13_divisor_l_output,
       division_circuit_block_13_input_output, division_circuit_block_13_output_value,
       division_circuit_block_14_divisor_h_output, division_circuit_block_14_divisor_l_output,
       division_circuit_block_14_input_output, division_circuit_block_14_output_value,
       division_circuit_block_15_divisor_h_output, division_circuit_block_15_divisor_l_output,
       division_circuit_block_15_input_output, division_circuit_block_15_output_value,
       division_circuit_block_16_divisor_h_output, division_circuit_block_16_divisor_l_output,
       division_circuit_block_16_input_output, division_circuit_block_16_output_value;

  // Probe on divisor
  // Probe on \input 
  // Probe on \output 
  division_circuit_block division_circuit_block_1 (
    .\output (division_circuit_block_2_output_value), .\input (division_circuit_block_2_input_output),
    .divisor_h(division_circuit_block_2_divisor_h_output),
    .divisor_l(division_circuit_block_2_divisor_l_output),
    .output_value(division_circuit_block_1_output_value),
    .input_output(division_circuit_block_1_input_output),
    .divisor_h_output(division_circuit_block_1_divisor_h_output),
    .divisor_l_output(division_circuit_block_1_divisor_l_output));
  division_circuit_block division_circuit_block_2 (
    .\output ({16{1'b0}}), .\input (\input ), .divisor_h({16{1'b0}}), .divisor_l(divisor),
    .output_value(division_circuit_block_2_output_value),
    .input_output(division_circuit_block_2_input_output),
    .divisor_h_output(division_circuit_block_2_divisor_h_output),
    .divisor_l_output(division_circuit_block_2_divisor_l_output));
  division_circuit_block division_circuit_block_3 (
    .\output (division_circuit_block_4_output_value), .\input (division_circuit_block_4_input_output),
    .divisor_h(division_circuit_block_4_divisor_h_output),
    .divisor_l(division_circuit_block_4_divisor_l_output),
    .output_value(division_circuit_block_3_output_value),
    .input_output(division_circuit_block_3_input_output),
    .divisor_h_output(division_circuit_block_3_divisor_h_output),
    .divisor_l_output(division_circuit_block_3_divisor_l_output));
  division_circuit_block division_circuit_block_4 (
    .\output (division_circuit_block_1_output_value), .\input (division_circuit_block_1_input_output),
    .divisor_h(division_circuit_block_1_divisor_h_output),
    .divisor_l(division_circuit_block_1_divisor_l_output),
    .output_value(division_circuit_block_4_output_value),
    .input_output(division_circuit_block_4_input_output),
    .divisor_h_output(division_circuit_block_4_divisor_h_output),
    .divisor_l_output(division_circuit_block_4_divisor_l_output));
  division_circuit_block division_circuit_block_5 (
    .\output (division_circuit_block_6_output_value), .\input (division_circuit_block_6_input_output),
    .divisor_h(division_circuit_block_6_divisor_h_output),
    .divisor_l(division_circuit_block_6_divisor_l_output),
    .output_value(division_circuit_block_5_output_value),
    .input_output(division_circuit_block_5_input_output),
    .divisor_h_output(division_circuit_block_5_divisor_h_output),
    .divisor_l_output(division_circuit_block_5_divisor_l_output));
  division_circuit_block division_circuit_block_6 (
    .\output (division_circuit_block_3_output_value), .\input (division_circuit_block_3_input_output),
    .divisor_h(division_circuit_block_3_divisor_h_output),
    .divisor_l(division_circuit_block_3_divisor_l_output),
    .output_value(division_circuit_block_6_output_value),
    .input_output(division_circuit_block_6_input_output),
    .divisor_h_output(division_circuit_block_6_divisor_h_output),
    .divisor_l_output(division_circuit_block_6_divisor_l_output));
  division_circuit_block division_circuit_block_7 (
    .\output (division_circuit_block_8_output_value), .\input (division_circuit_block_8_input_output),
    .divisor_h(division_circuit_block_8_divisor_h_output),
    .divisor_l(division_circuit_block_8_divisor_l_output),
    .output_value(division_circuit_block_7_output_value),
    .input_output(division_circuit_block_7_input_output),
    .divisor_h_output(division_circuit_block_7_divisor_h_output),
    .divisor_l_output(division_circuit_block_7_divisor_l_output));
  division_circuit_block division_circuit_block_8 (
    .\output (division_circuit_block_5_output_value), .\input (division_circuit_block_5_input_output),
    .divisor_h(division_circuit_block_5_divisor_h_output),
    .divisor_l(division_circuit_block_5_divisor_l_output),
    .output_value(division_circuit_block_8_output_value),
    .input_output(division_circuit_block_8_input_output),
    .divisor_h_output(division_circuit_block_8_divisor_h_output),
    .divisor_l_output(division_circuit_block_8_divisor_l_output));
  division_circuit_block division_circuit_block_9 (
    .\output (division_circuit_block_7_output_value), .\input (division_circuit_block_7_input_output),
    .divisor_h(division_circuit_block_7_divisor_h_output),
    .divisor_l(division_circuit_block_7_divisor_l_output),
    .output_value(division_circuit_block_9_output_value),
    .input_output(division_circuit_block_9_input_output),
    .divisor_h_output(division_circuit_block_9_divisor_h_output),
    .divisor_l_output(division_circuit_block_9_divisor_l_output));
  division_circuit_block division_circuit_block_10 (
    .\output (division_circuit_block_9_output_value), .\input (division_circuit_block_9_input_output),
    .divisor_h(division_circuit_block_9_divisor_h_output),
    .divisor_l(division_circuit_block_9_divisor_l_output),
    .output_value(division_circuit_block_10_output_value),
    .input_output(division_circuit_block_10_input_output),
    .divisor_h_output(division_circuit_block_10_divisor_h_output),
    .divisor_l_output(division_circuit_block_10_divisor_l_output));
  division_circuit_block division_circuit_block_11 (
    .\output (division_circuit_block_10_output_value), .\input (division_circuit_block_10_input_output),
    .divisor_h(division_circuit_block_10_divisor_h_output),
    .divisor_l(division_circuit_block_10_divisor_l_output),
    .output_value(division_circuit_block_11_output_value),
    .input_output(division_circuit_block_11_input_output),
    .divisor_h_output(division_circuit_block_11_divisor_h_output),
    .divisor_l_output(division_circuit_block_11_divisor_l_output));
  division_circuit_block division_circuit_block_12 (
    .\output (division_circuit_block_11_output_value), .\input (division_circuit_block_11_input_output),
    .divisor_h(division_circuit_block_11_divisor_h_output),
    .divisor_l(division_circuit_block_11_divisor_l_output),
    .output_value(division_circuit_block_12_output_value),
    .input_output(division_circuit_block_12_input_output),
    .divisor_h_output(division_circuit_block_12_divisor_h_output),
    .divisor_l_output(division_circuit_block_12_divisor_l_output));
  division_circuit_block division_circuit_block_13 (
    .\output (division_circuit_block_12_output_value), .\input (division_circuit_block_12_input_output),
    .divisor_h(division_circuit_block_12_divisor_h_output),
    .divisor_l(division_circuit_block_12_divisor_l_output),
    .output_value(division_circuit_block_13_output_value),
    .input_output(division_circuit_block_13_input_output),
    .divisor_h_output(division_circuit_block_13_divisor_h_output),
    .divisor_l_output(division_circuit_block_13_divisor_l_output));
  division_circuit_block division_circuit_block_14 (
    .\output (division_circuit_block_13_output_value), .\input (division_circuit_block_13_input_output),
    .divisor_h(division_circuit_block_13_divisor_h_output),
    .divisor_l(division_circuit_block_13_divisor_l_output),
    .output_value(division_circuit_block_14_output_value),
    .input_output(division_circuit_block_14_input_output),
    .divisor_h_output(division_circuit_block_14_divisor_h_output),
    .divisor_l_output(division_circuit_block_14_divisor_l_output));
  division_circuit_block division_circuit_block_15 (
    .\output (division_circuit_block_14_output_value), .\input (division_circuit_block_14_input_output),
    .divisor_h(division_circuit_block_14_divisor_h_output),
    .divisor_l(division_circuit_block_14_divisor_l_output),
    .output_value(division_circuit_block_15_output_value),
    .input_output(division_circuit_block_15_input_output),
    .divisor_h_output(division_circuit_block_15_divisor_h_output),
    .divisor_l_output(division_circuit_block_15_divisor_l_output));
  division_circuit_block division_circuit_block_16 (
    .\output (division_circuit_block_15_output_value), .\input (division_circuit_block_15_input_output),
    .divisor_h(division_circuit_block_15_divisor_h_output),
    .divisor_l(division_circuit_block_15_divisor_l_output),
    .output_value(division_circuit_block_16_output_value),
    .input_output(division_circuit_block_16_input_output),
    .divisor_h_output(division_circuit_block_16_divisor_h_output),
    .divisor_l_output(division_circuit_block_16_divisor_l_output));
  division_circuit_block division_circuit_block_17 (
    .\output (division_circuit_block_16_output_value), .\input (division_circuit_block_16_input_output),
    .divisor_h(division_circuit_block_16_divisor_h_output),
    .divisor_l(division_circuit_block_16_divisor_l_output), .output_value(\output ));  // open: input_output, divisor_h_output, divisor_l_output
endmodule

module registers (
  input  in_1,
  input  [15:0] in_2,
  input  [15:0] in_3,
  input  [7:0] in_4,
  input  in_5,
  input  in_6,
  input  in_7,
  output [15:0] out_8,
  output [15:0] out_9,
  output [15:0] out_10,
  output [15:0] out_11
);

  wire carry, imr_out_to_a, imr_out_to_b, ir_out_to_a, ir_out_to_b, iren, mar_out_to_a, mar_out_to_b,
       mdr_out_to_a, mdr_out_to_b, negative, pc_out_to_a, pc_out_to_b, reg_0_out_to_a, reg_0_out_to_b,
       reg_1_out_to_a, reg_1_out_to_b, reg_2_out_to_a, reg_2_out_to_b, reg_3_out_to_a, reg_3_out_to_b,
       reg_4_out_to_a, reg_4_out_to_b, reg_5_out_to_a, reg_5_out_to_b, reg_6_out_to_a, reg_6_out_to_b,
       reg_7_out_to_a, reg_7_out_to_b, reg_14_out_to_a, reg_14_out_to_b, sp_out_to_a, sp_out_to_b,
       stat_out_to_a, stat_out_to_b, zero;
  wire [15:0] immediate_value_q, memory_address_register_q, memory_data_register_q, program_counter_q, r0_q,
       r1_q, r2_q, r3_q, r4_q, r5_q, r6_q, r7_q, r14_q, stack_pointer_q, status_register_q;

  Decoder #(.select(4)) decoder_1 (
    .out0(reg_0_out_to_a), .out1(reg_1_out_to_a), .out2(reg_2_out_to_a), .out3(reg_3_out_to_a),
    .out4(reg_4_out_to_a), .out5(reg_5_out_to_a), .out6(reg_6_out_to_a), .out7(reg_7_out_to_a),
    .out8(pc_out_to_a), .out9(sp_out_to_a), .out10(stat_out_to_a), .out11(ir_out_to_a), .out12(mar_out_to_a),
    .out13(mdr_out_to_a), .out14(reg_14_out_to_a), .out15(imr_out_to_a), .sel(in_2[7:4]));  // open: en
  Decoder #(.select(4)) decoder_2 (
    .out0(reg_0_out_to_b), .out1(reg_1_out_to_b), .out2(reg_2_out_to_b), .out3(reg_3_out_to_b),
    .out4(reg_4_out_to_b), .out5(reg_5_out_to_b), .out6(reg_6_out_to_b), .out7(reg_7_out_to_b),
    .out8(pc_out_to_b), .out9(sp_out_to_b), .out10(stat_out_to_b), .out11(ir_out_to_b), .out12(mar_out_to_b),
    .out13(mdr_out_to_b), .out14(reg_14_out_to_b), .out15(imr_out_to_b), .sel(in_2[3:0]));  // open: en
  Register #(.width(16), .Select("low")) r0 (.D(in_3), .Q(r0_q), .clk(in_1));  // open: en, clr
  Register #(.width(16), .Select("low")) r1 (.D(in_3), .Q(r1_q), .clk(in_1));  // open: en, clr
  Register #(.width(16), .Select("low")) r2 (.D(in_3), .Q(r2_q), .clk(in_1));  // open: en, clr
  Register #(.width(16), .Select("low")) r3 (.D(in_3), .Q(r3_q), .clk(in_1));  // open: en, clr
  Register #(.width(16), .Select("low")) r4 (.D(in_3), .Q(r4_q), .clk(in_1));  // open: en, clr
  Register #(.width(16), .Select("low")) r5 (.D(in_3), .Q(r5_q), .clk(in_1));  // open: en, clr
  Register #(.width(16), .Select("low")) r6 (.D(in_3), .Q(r6_q), .clk(in_1));  // open: en, clr
  Register #(.width(16), .Select("low")) r7 (.D(in_3), .Q(r7_q), .clk(in_1));  // open: en, clr
  Counter #(.width(16), .max('hffff)) program_counter (
    .D(in_3), .Q(program_counter_q), .clk(in_1));  // open: load, count, carry, clr, preset, down
  Counter #(.width(16), .max('hffff)) stack_pointer (
    .D(in_3), .Q(stack_pointer_q), .clk(in_1));  // open: load, count, carry, clr, preset, down
  status_register status_register (
    .c(in_5), .z(in_7), .n(in_6), .q(status_register_q), .c_out(carry), .z_out(zero), .n_out(negative),
    .iren_out(iren));  // open: data, clock, iren, write_status, enable
  Register #(.width(16), .Select("low")) instruction_register (.D(in_3), .Q(in_2), .clk(in_1));  // open: en, clr
  Register #(.width(16), .Select("low")) memory_address_register (
    .D(in_3), .Q(memory_address_register_q), .clk(in_1));  // open: en, clr
  Register #(.width(16), .Select("low")) memory_data_register (
    .D(in_3), .Q(memory_data_register_q), .clk(in_1));  // open: en, clr
  Register #(.width(16), .Select("low")) r14 (.D(in_3), .Q(r14_q), .clk(in_1));  // open: en, clr
  Register #(.width(16), .Select("low")) immediate_value (
    .D(in_3), .Q(immediate_value_q), .clk(in_1));  // open: en, clr
  assign out_8 = reg_7_out_to_a ? r7_q : 16'bz;  // Controlled_Buffer controlled_buffer_1
  assign out_9 = reg_7_out_to_b ? r7_q : 16'bz;  // Controlled_Buffer controlled_buffer_2
  assign out_8 = pc_out_to_a ? program_counter_q : 16'bz;  // Controlled_Buffer controlled_buffer_3
  assign out_9 = pc_out_to_b ? program_counter_q : 16'bz;  // Controlled_Buffer controlled_buffer_4
  assign out_8 = sp_out_to_a ? stack_pointer_q : 16'bz;  // Controlled_Buffer controlled_buffer_5
  assign out_9 = sp_out_to_b ? stack_pointer_q : 16'bz;  // Controlled_Buffer controlled_buffer_6
  assign out_8 = mar_out_to_a ? memory_address_register_q : 16'bz;  // Controlled_Buffer controlled_buffer_7
  assign out_9 = mar_out_to_b ? memory_address_register_q : 16'bz;  // Controlled_Buffer controlled_buffer_8
  assign out_8 = mdr_out_to_a ? memory_data_register_q : 16'bz;  // Controlled_Buffer controlled_buffer_9
  assign out_9 = mdr_out_to_b ? memory_data_register_q : 16'bz;  // Controlled_Buffer controlled_buffer_10
  assign out_8 = reg_14_out_to_a ? r14_q : 16'bz;  // Controlled_Buffer controlled_buffer_11
  assign out_9 = reg_14_out_to_b ? r14_q : 16'bz;  // Controlled_Buffer controlled_buffer_12
  assign out_8 = imr_out_to_a ? immediate_value_q : 16'bz;  // Controlled_Buffer controlled_buffer_13
  assign out_9 = imr_out_to_b ? immediate_value_q : 16'bz;  // Controlled_Buffer controlled_buffer_14
  assign out_8 = reg_0_out_to_a ? r0_q : 16'bz;  // Controlled_Buffer controlled_buffer_15
  assign out_9 = reg_0_out_to_b ? r0_q : 16'bz;  // Controlled_Buffer controlled_buffer_16
  assign out_8 = reg_1_out_to_a ? r1_q : 16'bz;  // Controlled_Buffer controlled_buffer_17
  assign out_9 = reg_1_out_to_b ? r1_q : 16'bz;  // Controlled_Buffer controlled_buffer_18
  assign out_8 = reg_2_out_to_a ? r2_q : 16'bz;  // Controlled_Buffer controlled_buffer_19
  assign out_9 = reg_2_out_to_b ? r2_q : 16'bz;  // Controlled_Buffer controlled_buffer_20
  assign out_8 = reg_3_out_to_a ? r3_q : 16'bz;  // Controlled_Buffer controlled_buffer_21
  assign out_9 = reg_3_out_to_b ? r3_q : 16'bz;  // Controlled_Buffer controlled_buffer_22
  assign out_8 = reg_4_out_to_a ? r4_q : 16'bz;  // Controlled_Buffer controlled_buffer_23
  assign out_9 = reg_4_out_to_b ? r4_q : 16'bz;  // Controlled_Buffer controlled_buffer_24
  assign out_8 = reg_5_out_to_a ? r5_q : 16'bz;  // Controlled_Buffer controlled_buffer_25
  assign out_9 = reg_5_out_to_b ? r5_q : 16'bz;  // Controlled_Buffer controlled_buffer_26
  assign out_8 = reg_6_out_to_a ? r6_q : 16'bz;  // Controlled_Buffer controlled_buffer_27
  assign out_9 = reg_6_out_to_b ? r6_q : 16'bz;  // Controlled_Buffer controlled_buffer_28
  assign out_8 = stat_out_to_a ? status_register_q : 16'bz;  // Controlled_Buffer controlled_buffer_29
  assign out_9 = stat_out_to_b ? status_register_q : 16'bz;  // Controlled_Buffer controlled_buffer_30
  assign out_8 = ir_out_to_a ? in_2 : 16'bz;  // Controlled_Buffer controlled_buffer_31
  assign out_9 = ir_out_to_b ? in_2 : 16'bz;  // Controlled_Buffer controlled_buffer_32

  assign in_4 = in_2[15:8];

  // Other names for the same wires on the sheet: a_bus[15:0] = out_8; b_bus[15:0] = out_9; c_bus[15:0] = in_3;
  //   carry_in = in_5; clock = in_1; instruction_register[15:0] = in_2; instruction[7:0] = in_2[15:8];
  //   negative_in = in_6; zero_in = in_7

  // Notes on the sheet:
  //   reg1
  //   reg2
  //   first 8 bits are instruction, next 4 are reg1 final 4 are reg 2
endmodule
